// Logisim project 4_bit_adder.circ as structural Verilog: 10 circuits, main circuit top
module add2 (
  input  in_1,
  input  in_2,
  input  in_3,
  output out_4,
  output out_5
);

  wire and_1_out, and_2_out, and_3_out;

  xor xor_1 (out_5, in_1, in_2, in_3);
  and and_1 (and_1_out, in_1, in_2);
  and and_2 (and_2_out, in_1, in_3);
  and and_3 (and_3_out, in_2, in_3);
  or or_1 (out_4, and_1_out, and_2_out, and_3_out);
endmodule

module add4 (
  input  [3:0] in_1,
  input  [3:0] in_2,
  input  in_3,
  output out_4,
  output [3:0] out_5
);

  wire add2_2_out_4, add2_3_out_4, add2_4_out_4;

  add2 add2_1 (.in_1(in_1[3]), .in_2(in_2[3]), .in_3(add2_2_out_4), .out_4(out_4), .out_5(out_5[3]));
  add2 add2_2 (.in_1(in_1[2]), .in_2(in_2[2]), .in_3(add2_3_out_4), .out_4(add2_2_out_4), .out_5(out_5[2]));
  add2 add2_3 (.in_1(in_1[1]), .in_2(in_2[1]), .in_3(add2_4_out_4), .out_4(add2_3_out_4), .out_5(out_5[1]));
  add2 add2_4 (.in_1(in_1[0]), .in_2(in_2[0]), .in_3(in_3), .out_4(add2_4_out_4), .out_5(out_5[0]));
endmodule

module flipper (
  input  in_1,
  input  in_2,
  input  in_3,
  input  in_4,
  input  in_5,
  output out_6,
  output out_7,
  output out_8,
  output out_9
);

  xor xor_1 (out_6, in_1, in_5);
  xor xor_2 (out_7, in_2, in_5);
  xor xor_3 (out_8, in_3, in_5);
  xor xor_4 (out_9, in_4, in_5);
endmodule

module add8 (
  input  [7:0] in_1,
  input  [7:0] in_2,
  input  in_3,
  output out_4,
  output [7:0] out_5
);

  wire add4_2_out_4;

  add4 add4_1 (.in_1(in_1[7:4]), .in_2(in_2[7:4]), .in_3(add4_2_out_4), .out_4(out_4), .out_5(out_5[7:4]));
  add4 add4_2 (.in_1(in_1[3:0]), .in_2(in_2[3:0]), .in_3(in_3), .out_4(add4_2_out_4), .out_5(out_5[3:0]));
endmodule

module alu8 (
  input  right_shift_logical,
  input  left_shift_logical,
  input  \xor ,
  input  \or ,
  input  \and ,
  input  add_subtract,
  input  subtract,
  input  [7:0] b,
  input  [7:0] a,
  output [7:0] out_10,
  output carry_out
);

  wire [7:0] adder_1_out, and_1_out, bit_extender_1_out, left_shift_1_out_2, or_1_out, right_shift_1_out_2,
       xor_1_out, xor_2_out;

  assign bit_extender_1_out = {{7{subtract}}, subtract};  // Bit_Extender bit_extender_1
  assign xor_1_out = bit_extender_1_out ^ b;  // XOR_Gate xor_1, 8 bits wide
  assign and_1_out = b & a;  // AND_Gate and_1, 8 bits wide
  assign or_1_out = b | a;  // OR_Gate or_1, 8 bits wide
  assign xor_2_out = b ^ a;  // XOR_Gate xor_2, 8 bits wide
  left_shift left_shift_1 (.in_1(a), .out_2(left_shift_1_out_2));
  right_shift right_shift_1 (.in_1(a), .out_2(right_shift_1_out_2));
  Adder adder_1 (.a(xor_1_out), .b(a), .out(adder_1_out), .cin(subtract), .cout(carry_out));
  assign out_10 = add_subtract ? adder_1_out : 8'bz;  // Controlled_Buffer controlled_buffer_1
  assign out_10 = \and  ? and_1_out : 8'bz;  // Controlled_Buffer controlled_buffer_2
  assign out_10 = \or  ? or_1_out : 8'bz;  // Controlled_Buffer controlled_buffer_3
  assign out_10 = \xor  ? xor_2_out : 8'bz;  // Controlled_Buffer controlled_buffer_4
  assign out_10 = left_shift_logical ? left_shift_1_out_2 : 8'bz;  // Controlled_Buffer controlled_buffer_5
  assign out_10 = right_shift_logical ? right_shift_1_out_2 : 8'bz;  // Controlled_Buffer controlled_buffer_6
endmodule

module left_shift (
  input  [7:0] in_1,
  output [7:0] out_2
);


  assign out_2 = {in_1[6:0], 1'b0};
endmodule

module right_shift (
  input  [7:0] in_1,
  output [7:0] out_2
);


  assign out_2 = {1'b0, in_1[7:1]};
endmodule

module top (
  input  [7:0] in_1,
  input  in_2,
  input  in_3,
  input  in_4,
  input  in_5,
  input  in_6,
  input  enable,
  input  in_8,
  input  in_9,
  input  enable_2,
  input  in_11,
  input  clock,
  input  in_13,
  input  in_14,
  input  in_15,
  input  in_16,
  input  in_17,
  output out_18,
  output [7:0] out_19
);

  wire [7:0] controlled_buffer_1_out, controlled_buffer_3_out, register_1_q, register_2_q;

  Register register_1 (.D(out_19), .en(enable), .Q(register_1_q), .clk(clock), .clr(in_13));
  Register register_2 (.D(out_19), .en(enable_2), .Q(register_2_q), .clk(clock), .clr(in_13));
  assign controlled_buffer_1_out = in_2 ? in_1 : 8'bz;  // Controlled_Buffer controlled_buffer_1
  assign controlled_buffer_1_out = in_14 ? register_1_q : 8'bz;  // Controlled_Buffer controlled_buffer_2
  assign controlled_buffer_3_out = in_15 ? register_1_q : 8'bz;  // Controlled_Buffer controlled_buffer_3
  assign controlled_buffer_1_out = in_16 ? register_2_q : 8'bz;  // Controlled_Buffer controlled_buffer_4
  assign controlled_buffer_3_out = in_17 ? register_2_q : 8'bz;  // Controlled_Buffer controlled_buffer_5
  alu8 alu8_1 (
    .right_shift_logical(in_11), .left_shift_logical(in_9), .\xor (in_8), .\or (in_6), .\and (in_5),
    .add_subtract(in_4), .subtract(in_3), .b(controlled_buffer_3_out), .a(controlled_buffer_1_out),
    .out_10(out_19), .carry_out(out_18));

  // Notes on the sheet:
  //   reset all registers
endmodule

module latch (
  input  in_1,
  input  in_2,
  input  in_3,
  output out_4
);

  wire and_1_out, and_2_out, nor_1_out, not_1_out, or_1_out;

  not not_1 (not_1_out, in_1);
  and and_1 (and_1_out, in_1, in_2);
  and and_2 (and_2_out, in_2, not_1_out);
  or or_1 (or_1_out, and_2_out, in_3);
  nor nor_1 (nor_1_out, and_1_out, out_4);
  nor nor_2 (out_4, nor_1_out, or_1_out);
endmodule

module falling_edge_triggered_d_triggered_flip_flop (
  input  in_1,
  input  in_2,
  input  in_3,
  output out_4
);

  wire latch_1_out_4, not_1_out;

  latch latch_1 (.in_1(in_1), .in_2(in_2), .out_4(latch_1_out_4), .in_3(in_3));
  not not_1 (not_1_out, in_2);
  latch latch_2 (.in_1(latch_1_out_4), .in_2(not_1_out), .out_4(out_4), .in_3(in_3));
endmodule
